// Digital circuit 8_Bit_Register.dig as structural Verilog
module _8_Bit_Register (
  input  [7:0] D_IN,
  input  EN,
  input  CLK,
  input  RST,
  output [7:0] D_OUT
);

  wire and_1_out, d_ff_1_q;

  D_FF d_ff_1 (.D(EN), .C(CLK), .Q(d_ff_1_q));  // open: nQ
  and and_1 (and_1_out, d_ff_1_q, CLK);
  D_FF_AS d_ff_as_1 (.Set(1'b0), .D(D_IN[0]), .C(and_1_out), .Clr(RST), .Q(D_OUT[0]));  // open: nQ
  D_FF_AS d_ff_as_2 (.Set(1'b0), .D(D_IN[1]), .C(and_1_out), .Clr(RST), .Q(D_OUT[1]));  // open: nQ
  D_FF_AS d_ff_as_3 (.Set(1'b0), .D(D_IN[2]), .C(and_1_out), .Clr(RST), .Q(D_OUT[2]));  // open: nQ
  D_FF_AS d_ff_as_4 (.Set(1'b0), .D(D_IN[3]), .C(and_1_out), .Clr(RST), .Q(D_OUT[3]));  // open: nQ
  D_FF_AS d_ff_as_5 (.Set(1'b0), .D(D_IN[4]), .C(and_1_out), .Clr(RST), .Q(D_OUT[4]));  // open: nQ
  D_FF_AS d_ff_as_6 (.Set(1'b0), .D(D_IN[5]), .C(and_1_out), .Clr(RST), .Q(D_OUT[5]));  // open: nQ
  D_FF_AS d_ff_as_7 (.Set(1'b0), .D(D_IN[6]), .C(and_1_out), .Clr(RST), .Q(D_OUT[6]));  // open: nQ
  D_FF_AS d_ff_as_8 (.Set(1'b0), .D(D_IN[7]), .C(and_1_out), .Clr(RST), .Q(D_OUT[7]));  // open: nQ
endmodule
