// Digital circuit Gesammtprojekt.dig as structural Verilog
module Gesammtprojekt (
  input  clk,
  input  in_2,
  input  in_3,
  input  in_4,
  input  in_5,
  input  in_6,
  input  in_7,
  input  in_8,
  input  in_9,
  input  in_10,
  input  in_11,
  input  in_12
);

  wire sequencer_1_execute, sequencer_1_fetch_dr, sequencer_1_fetch_ir;
  wire [3:0] \zähler_1_q_0 ;
  wire [7:0] _8_bit_register_1_d_out;

  \Zähler  \zähler_1  (
    .CLK(clk), .q_0(\zähler_1_q_0 [0]), .q_1(\zähler_1_q_0 [1]), .q_2(\zähler_1_q_0 [2]),
    .q_3(\zähler_1_q_0 [3]));
  LED led_1 (.in(\zähler_1_q_0 [0]));
  LED led_2 (.in(\zähler_1_q_0 [1]));
  Seven_Seg_Hex seven_seg_hex_1 (.d(\zähler_1_q_0 ), .dp(1'b0));
  LED led_3 (.in(\zähler_1_q_0 [2]));
  LED led_4 (.in(\zähler_1_q_0 [3]));
  _8_Bit_Register _8_bit_register_1 (
    .D_IN({in_9, in_8, in_7, in_6, in_5, in_4, in_3, in_2}), .EN(in_10), .CLK(clk), .RST(in_11),
    .D_OUT(_8_bit_register_1_d_out));
  LED led_5 (.in(_8_bit_register_1_d_out[0]));
  LED led_6 (.in(_8_bit_register_1_d_out[1]));
  LED led_7 (.in(_8_bit_register_1_d_out[2]));
  LED led_8 (.in(_8_bit_register_1_d_out[3]));
  LED led_9 (.in(_8_bit_register_1_d_out[4]));
  LED led_10 (.in(_8_bit_register_1_d_out[5]));
  LED led_11 (.in(_8_bit_register_1_d_out[6]));
  LED led_12 (.in(_8_bit_register_1_d_out[7]));
  Sequencer sequencer_1 (
    .CLK(clk), .RST(in_12), .Fetch_IR(sequencer_1_fetch_ir), .Fetch_DR(sequencer_1_fetch_dr),
    .Execute(sequencer_1_execute));
  LED led_13 (.in(sequencer_1_fetch_ir));
  LED led_14 (.in(sequencer_1_fetch_dr));
  LED led_15 (.in(sequencer_1_execute));

  // Notes on the sheet:
  //   Aufgabe 1
  //   Aufgabe 2
  //   Aufgabe 3
endmodule
