// Digital circuit Sequencer.dig as structural Verilog
module Sequencer (
  input  CLK,
  input  RST,
  output Fetch_IR,
  output Fetch_DR,
  output Execute
);

  wire and_4_out, d_ff_as_1_q, d_ff_as_2_q, not_1_out, or_1_out, xor_1_out;

  not not_1 (not_1_out, d_ff_as_1_q);
  D_FF_AS d_ff_as_1 (.Set(1'b0), .D(not_1_out), .C(CLK), .Clr(or_1_out), .Q(d_ff_as_1_q));  // open: nQ
  and and_1 (Fetch_IR, ~d_ff_as_2_q, ~d_ff_as_1_q);  // And
  xor xor_1 (xor_1_out, d_ff_as_1_q, d_ff_as_2_q);
  and and_2 (Fetch_DR, ~d_ff_as_2_q, d_ff_as_1_q);  // And
  and and_3 (Execute, d_ff_as_2_q, ~d_ff_as_1_q);  // And
  D_FF_AS d_ff_as_2 (.Set(1'b0), .D(xor_1_out), .C(CLK), .Clr(or_1_out), .Q(d_ff_as_2_q));  // open: nQ
  and and_4 (and_4_out, d_ff_as_2_q, d_ff_as_1_q);
  or or_1 (or_1_out, and_4_out, RST);
endmodule
