// Digital circuit Zähler.dig as structural Verilog
module \Zähler  (
  input  CLK,
  output q_0,
  output q_1,
  output q_2,
  output q_3
);

  wire and_1_out, and_2_out, and_3_out, not_1_out, xor_1_out, xor_2_out, xor_3_out;

  and and_1 (and_1_out, ~q_0, q_1, ~q_2, q_3);  // And
  not not_1 (not_1_out, q_0);
  D_FF_AS d_ff_as_1 (.Set(1'b0), .D(not_1_out), .C(CLK), .Clr(and_1_out), .Q(q_0));  // open: nQ
  xor xor_1 (xor_1_out, q_0, q_1);
  D_FF_AS d_ff_as_2 (.Set(1'b0), .D(xor_1_out), .C(CLK), .Clr(and_1_out), .Q(q_1));  // open: nQ
  and and_2 (and_2_out, q_1, q_0);
  xor xor_2 (xor_2_out, and_2_out, q_2);
  D_FF_AS d_ff_as_3 (.Set(1'b0), .D(xor_2_out), .C(CLK), .Clr(and_1_out), .Q(q_2));  // open: nQ
  and and_3 (and_3_out, q_2, q_1, q_0);
  xor xor_3 (xor_3_out, and_3_out, q_3);
  D_FF_AS d_ff_as_4 (.Set(1'b0), .D(xor_3_out), .C(CLK), .Clr(and_1_out), .Q(q_3));  // open: nQ
endmodule
